# Fritzing sketch DO_NHIET_DO (saved by Fritzing 0.9.2b)
circuit board: 5.64655cm x 5.22442cm
breadboards: 1

parts:
  Part1 = Arduino Pro Mini v13
  7805 = Voltage Regulator - 5V [package="TO220 [THT]"]
  NGUON = Screw terminal - 2 pins [package=THT]
  C1 = Electrolytic Capacitor [capacitance=1µF package="100 mil [THT, electrolytic]"]
  R1 = Resistor [tolerance=±5% resistance=220 package=THT]
  LED1 = LED - 5mm [color="Red (633nm)" package="5 mm [THT]"]
  SG1 = Buzzer 12mm [package=buzzer-12mm-ns]
  R2 = Resistor [tolerance=±5% resistance=220 package=THT]
  DS12B20 = female pin header, 3 pins [form="♀ (female)"]
  R3 = Resistor [tolerance=±5% resistance=220 package=THT]
  S2 = Momentary Switch [package=tactile-pth]
  S3 = Momentary Switch [package=tactile-pth]
  S4 = Momentary Switch [package=tactile-pth]
  S5 = Momentary Switch [package=tactile-pth]
  R4 = Resistor [tolerance=±5% resistance=220 package=THT]
  R5 = Resistor [tolerance=±5% resistance=220 package=THT]
  R6 = Resistor [tolerance=±5% resistance=220 package=THT]
  J1 = female pin header, 2 pins [form="♀ (female)"]  # not connected

nets:
  N1: Part1.VCC, 7805.output_voltage, C1.+, R1.Pin_1, DS12B20.pin3
  GND: Part1.GND, 7805.GND, NGUON.pin2, C1.-, LED1.cathode, SG1.2, DS12B20.pin1, S2.3, S3.4, S4.4, S5.4
  D3: Part1.D3_PWM, R2.Pin_0
  N2: Part1.D2, DS12B20.pin2
  5V: 7805.input_voltage, NGUON.pin1, R3.Pin_0, R4.Pin_0, R5.Pin_0, R6.Pin_0
  N3: R1.Pin_0, LED1.anode
  N4: SG1.1, R2.Pin_1
  N5: R3.Pin_1, S2.2
  N6: S3.2, R4.Pin_1
  N7: S4.2, R6.Pin_1
  N8: S5.2, R5.Pin_1
